# Fritzing sketch schematic (saved by Fritzing 0.7.12b)
breadboards: 1

parts:
  IC1 = Microchip MCP23008 8-bit I/O expander [part_number=MCP23008 package="DIP (Dual Inline) [THT]"]
  IC2 = Microchip MCP23008 8-bit I/O expander [part_number=MCP23008 package="DIP (Dual Inline) [THT]"]
  IC3 = Microchip MCP23008 8-bit I/O expander [part_number=MCP23008 package="DIP (Dual Inline) [THT]"]
  Raspberry_Pi1 = Raspberry Pi (Model B)
  R1 = 330 Ω Resistor [package=THT]
  R2 = 330 Ω Resistor [package=THT]
  R3 = 330 Ω Resistor [package=THT]
  LED1 = green LED - 5mm [package="5 mm [THT]"]
  LED2 = green LED - 5mm [package="5 mm [THT]"]
  LED3 = green LED - 5mm [package="5 mm [THT]"]
  S1 = Reed switch [package=THT]
  S3 = Reed switch [package=THT]
  S4 = Reed switch [package=THT]
  S5 = Reed switch [package=THT]
  S6 = Reed switch [package=THT]
  S7 = Reed switch [package=THT]
  S8 = Reed switch [package=THT]
  S9 = Reed switch [package=THT]
  S10 = Reed switch [package=THT]
  S11 = Reed switch [package=THT]
  S12 = Reed switch [package=THT]
  S13 = Reed switch [package=THT]
  R4 = 1k Ω Resistor [package=THT]
  R5 = 1k Ω Resistor [package=THT]
  R6 = 1k Ω Resistor [package=THT]
  R7 = 1k Ω Resistor [package=THT]
  R8 = 1k Ω Resistor [package=THT]
  R9 = 1k Ω Resistor [package=THT]
  R10 = 1k Ω Resistor [package=THT]
  R11 = 1k Ω Resistor [package=THT]
  R12 = 1k Ω Resistor [package=THT]
  R13 = 1k Ω Resistor [package=THT]
  R14 = 1k Ω Resistor [package=THT]
  R15 = 1k Ω Resistor [package=THT]
  R16 = 1k Ω Resistor [package=THT]
  S2 = Reed switch [package=THT]

nets:
  N1: IC1.SCL, IC2.SCL, IC3.SCL, Raspberry_Pi1.SCL
  N2: IC1.SDA, IC2.SDA, IC3.SDA, Raspberry_Pi1.SDA
  VSS: IC1.A2, IC1.A1, IC1.A0, IC1.VSS, IC2.A2, IC2.A1, IC2.VSS, IC3.A2, IC3.A0, IC3.VSS, Raspberry_Pi1.GND, LED1.cathode, LED2.cathode, LED3.cathode, R4.Pin_0, R5.Pin_0, R6.Pin_0, R7.Pin_0, R8.Pin_0, R9.Pin_0, R10.Pin_0, R11.Pin_0, R12.Pin_0, R13.Pin_0, R14.Pin_0, R15.Pin_0, R16.Pin_0
  VDD: IC1.Reset, IC1.VDD, IC2.A0, IC2.Reset, IC2.VDD, IC3.A1, IC3.Reset, IC3.VDD, Raspberry_Pi1.5V, S1.pin_1, S3.pin_1, S4.pin_1, S5.pin_1, S6.pin_1, S7.pin_1, S8.pin_1, S9.pin_1, S10.pin_1, S11.pin_1, S12.pin_1, S13.pin_1, S2.pin_1
  N3: IC1.GP0, S6.pin_2, R10.Pin_1
  N4: IC1.GP1, S7.pin_2, R9.Pin_1
  N5: IC1.GP2, S8.pin_2, R8.Pin_1
  N6: IC1.GP3, S9.pin_2, R7.Pin_1
  N7: IC1.GP4, S10.pin_2, R11.Pin_1
  N8: IC1.GP5, S11.pin_2, R6.Pin_1
  N9: IC1.GP6, S12.pin_2, R5.Pin_1
  N10: IC1.GP7, S13.pin_2, R4.Pin_1
  N11: IC2.GP0, S1.pin_2, R12.Pin_1
  N12: IC2.GP1, R13.Pin_1, S2.pin_2
  N13: IC2.GP2, S3.pin_2, R14.Pin_1
  N14: IC2.GP3, S4.pin_2, R16.Pin_1
  N15: IC2.GP4, S5.pin_2, R15.Pin_1
  N16: IC3.GP0, R1.Pin_1
  N17: IC3.GP1, R2.Pin_1
  N18: IC3.GP2, R3.Pin_1
  N19: R1.Pin_0, LED1.anode
  N20: R2.Pin_0, LED2.anode
  N21: R3.Pin_0, LED3.anode

custom parts:
  Microchip MCP23008 8-bit I/O expander: Provides 8-bit, general purpose, parallel I/O expansion for I2C bus. Datasheet: http://ww1.microchip.com/downloads/en/devicedoc/21919e.pdf
  Raspberry Pi (Model B): Raspberry Pi Single-board Computer, Model B
